# Fritzing sketch Beepo (saved by Fritzing 0.9.3b)
circuit board: 8cm x 8cm

parts:
  LED1 = LED - 3mm [color="Green (565nm)" package="3 mm [THT]"]
  Pad1 = Pad [width=4 height=6 connect=center]
  Pad2 = Pad [width=4 height=6 connect=center]
  Pad3 = Pad [width=4 height=6 connect=center]
  Pad4 = Pad [width=4 height=6 connect=center]
  Pad5 = Pad [width=4 height=6 connect=center]
  Pad6 = Pad [width=4 height=6 connect=center]
  NE555 = General purpose bipolar Timer [package=dil-08]
  SPK = Piezo Speaker
  R1 = Resistor [tolerance=±5% resistance=220 package="1206 [SMD]"]
  R2 = Resistor [tolerance=±5% resistance=220 package="1206 [SMD]"]
  R3 = Resistor [tolerance=±5% resistance=220 package="1206 [SMD]"]
  R4 = Resistor [tolerance=±5% resistance=220 package="1206 [SMD]"]
  R5 = Resistor [tolerance=±5% resistance=220 package="1206 [SMD]"]
  R6 = Resistor [tolerance=±5% resistance=220 package="1206 [SMD]"]
  R7 = Resistor [tolerance=±5% resistance=220 package="1206 [SMD]"]
  R8 = Resistor [tolerance=±5% resistance=220 package="1206 [SMD]"]
  R9 = Resistor [tolerance=±5% resistance=220 package="1206 [SMD]"]
  R10 = Resistor [tolerance=±5% resistance=220 package="1206 [SMD]"]
  R12 = Resistor [tolerance=±5% resistance=220 package="1206 [SMD]"]
  POT = Trimmer Potentiometer [maximum_resistance=10kΩ package=THT]
  J1 = female pin header, 1 pin [form="♀ (female)"]
  C1 = Electrolytic Capacitor [capacitance=10µF package="0605 [SMD, electrolytic]"]
  R25 = Resistor [tolerance=±5% resistance=220 package="1206 [SMD]"]
  9V = Battery block 9V
  R26 = Resistor [tolerance=±5% resistance=220 package="1206 [SMD]"]
  Pad7 = Pad [width=4 height=6 connect=center]
  Pad8 = Pad [width=4 height=6 connect=center]
  Pad9 = Pad [width=4 height=6 connect=center]
  Pad10 = Pad [width=4 height=6 connect=center]
  Pad11 = Pad [width=4 height=6 connect=center]
  Pad12 = Pad [width=4 height=6 connect=center]

nets:
  N1: LED1.cathode, NE555.GND, SPK.pin1, 9V.-
  N2: LED1.anode, R25.Pin_0
  N3: Pad1.pad, R5.Pin_1, R6.Pin_0
  N4: Pad2.pad, R4.Pin_1, R5.Pin_0
  N5: Pad3.pad, R3.Pin_1, R4.Pin_0
  N6: Pad4.pad, R2.Pin_1, R3.Pin_0
  N7: Pad5.pad, R1.Pin_1, R2.Pin_0
  N8: Pad6.pad, R1.Pin_0, POT.leg2
  N9: NE555.TRI, NE555.TRE, J1.pin1
  N10: NE555.OUT, C1.+
  N11: NE555._RES, NE555.VCC+, R25.Pin_1, 9V.+, R26.Pin_1
  N12: NE555.DIS, POT.leg1, POT.wiper, R26.Pin_0
  N13: SPK.pin2, C1.-
  N14: R6.Pin_1, R12.Pin_0, Pad7.pad
  N15: R7.Pin_0, R9.Pin_1, Pad11.pad
  N16: R7.Pin_1, Pad12.pad
  N17: R8.Pin_0, R10.Pin_1, Pad9.pad
  N18: R8.Pin_1, R9.Pin_0, Pad10.pad
  N19: R10.Pin_0, R12.Pin_1, Pad8.pad
